# Fritzing sketch Skema_IR-Remote (saved by Fritzing 0.9.3b)

parts:
  Part1 = KY-022 Infrared Receiver Module [package="Breakout board"]
  Part2 = Arduino Uno (Rev3)

nets:
  N1: Part1.S, Part2.D8
  VIN: Part1.Vin, Part2.5V
  N2: Part1.-, Part2.GND

custom parts:
  KY-022 Infrared Receiver Module: Arduino IR receiver module KY-022, reacts to 38kHz infrared light.
