# Fritzing sketch Skema_Laser-Transmitter (saved by Fritzing 0.9.3b)

parts:
  KY-008_Laserdiode1 = Laser [part_number=1219301 package=keys]
  Part1 = Arduino Uno (Rev3)

nets:
  N1: KY-008_Laserdiode1.connector0pin, Part1.D10_PWM/SS
  N2: KY-008_Laserdiode1.connector1pin, Part1.5V
  N3: KY-008_Laserdiode1.connector2pin, Part1.GND

custom parts:
  Laser: KEYES KY-008 650nm Laser Transmitter Module
