# Fritzing sketch Skema_Relay (saved by Fritzing 0.9.3b)

parts:
  KY-1 = Keyes Relay [package=THT]
  Part1 = Arduino Uno (Rev3)
  LED1 = LEDs [package=led10mm]

nets:
  N1: KY-1.signal, Part1.D10_PWM/SS
  N2: KY-1.power, Part1.5V
  N3: KY-1.ground, Part1.GND
  N4: KY-1.C, LED1.A

custom parts:
  Keyes Relay: The Keyes 5V relay module is suitable for SCM development, home appliance control. It uses a 5V~12V TIL control signal which can control DC / AC signal.
  LEDs: LEDs Standard schematic elements and footprints for 5mm, 3mm, 1206, and 0603 sized LEDs. 5mm - Spark Fun Electronics SKU : COM-00529 (and others)
