# Fritzing sketch Skema_LDR (saved by Fritzing 0.9.3b)

parts:
  Part1 = Arduino Uno (Rev3)
  R1 = Photocell (LDR) [package=THT]
  R2 = Resistor [tolerance=±5% resistance=10k package=THT]

nets:
  N1: Part1.A1, R2.Pin_0
  N2: Part1.5V, R1.pin_0
  N3: Part1.GND, R2.Pin_1
