# Fritzing sketch Skema_Servo (saved by Fritzing 0.9.3b)

parts:
  J1 = Basic Servo
  Part1 = Arduino Uno (Rev3)

nets:
  GND: J1.gnd, Part1.GND
  VCC: J1.vcc, Part1.5V
  N1: J1.pulse, Part1.D10_PWM/SS
