# Fritzing sketch Seven-Segment (saved by Fritzing 0.9.3b)
breadboards: 1

parts:
  DI1 = 7-Segment LED Display [package=THT]
  R1 = Resistor [tolerance=±5% resistance=220 package=THT]
  Part1 = Arduino Uno (Rev3)

nets:
  N1: DI1.cathodeE, Part1.D6_PWM
  N2: DI1.cathodeD, Part1.D5_PWM
  N3: DI1.cathodeC, Part1.D4
  N4: DI1.cathodeDP, Part1.D9_PWM
  N5: DI1.cathodeB, Part1.D3_PWM
  N6: DI1.cathodeA, Part1.D2
  N7: DI1.commAnode#7, R1.Pin_0
  N8: DI1.cathodeF, Part1.D7
  N9: DI1.cathodeG, Part1.D8
  N10: R1.Pin_1, Part1.5V
